# Fritzing sketch reaction (saved by Fritzing 0.9.3b)
breadboards: 1

parts:
  Εξάρτημα1 = Arduino Uno (Rev3)
  J1 = Piezo Speaker
  U1 = TMP36 [package=to-92-kit]
  S1 = Momentary Switch [package=ksa_sealed_tac_switch]
  LED1 = RGB LED (com. cathode, rbg) [package="5 mm [THT]"]
  R1 = Resistor [tolerance=±5% resistance=220 package=THT]
  R2 = Resistor [tolerance=±5% resistance=220 package=THT]
  R3 = Resistor [tolerance=±5% resistance=220 package=THT]
  R4 = Resistor [tolerance=±5% resistance=10k package=THT]
  LCD1 = LCD screen
  R5 = Rotary Potentiometer (Small) [maximum_resistance=100kΩ package=THT]

nets:
  N1: Εξάρτημα1.A0, U1.VOUT
  N2: Εξάρτημα1.D9_PWM, R3.Pin_0
  N3: Εξάρτημα1.D10_PWM/SS, R2.Pin_0
  N4: Εξάρτημα1.D11_PWM/MOSI, R1.Pin_0
  N5: Εξάρτημα1.D12/MISO, LCD1.DB4
  N6: Εξάρτημα1.D13/SCK, LCD1.DB6
  GND: Εξάρτημα1.GND, J1.pin1, U1.GND, LED1.common_cathode, R4.Pin_1, LCD1.VSS, LCD1.DB5, LCD1.LED-, R5.leg2
  N7: Εξάρτημα1.D2, S1.3, R4.Pin_0
  N8: Εξάρτημα1.D3_PWM, J1.pin2
  N9: Εξάρτημα1.D4, LCD1.V0
  N10: Εξάρτημα1.D5_PWM, LCD1.RS
  N11: Εξάρτημα1.D6_PWM, LCD1.R/W
  N12: Εξάρτημα1.D7, LCD1.E
  5V: Εξάρτημα1.5V, U1.VCC, S1.1, LCD1.VDD, LCD1.LED+, R5.leg1
  N13: LED1.red_anode, R1.Pin_1
  N14: LED1.blue_anode, R2.Pin_1
  N15: LED1.green_anode, R3.Pin_1
  N16: LCD1.DB7, R5.wiper
